# Fritzing sketch diagram (saved by Fritzing 0.9.3b)
breadboards: 1

parts:
  Part1 = Arduino Nano (Rev3.0)
  J1 = Basic Servo
  J2 = Basic Servo
  J3 = Basic Force Sensing Resistor (FSR) [package=THT]
  J4 = Basic Force Sensing Resistor (FSR) [package=THT]
  J5 = Basic Force Sensing Resistor (FSR) [package=THT]
  J6 = Basic Force Sensing Resistor (FSR) [package=THT]
  R1 = Resistor [tolerance=±5% resistance=25k package="2010 [SMD]"]
  R2 = Resistor [tolerance=±5% resistance=25k package="2010 [SMD]"]
  R3 = Resistor [tolerance=±5% resistance=25k package="2010 [SMD]"]
  R4 = Resistor [tolerance=±5% resistance=25k package="2010 [SMD]"]
  VCC1 = 4 x AAA Battery Mount

nets:
  GND: Part1.GND, J1.gnd, J2.gnd, J3.pin_1, J4.pin_0, J5.pin_0, J6.pin_1, VCC1.-
  N1: Part1.D5, J2.pulse
  N2: Part1.D6, J1.pulse
  N3: Part1.5V, R1.Pin_0, R2.Pin_0, R3.Pin_0, R4.Pin_0
  N4: Part1.A7, J4.pin_1, R4.Pin_1
  N5: Part1.A5, J5.pin_1, R3.Pin_1
  N6: Part1.A3, J6.pin_0, R2.Pin_1
  N7: Part1.A1, Part1.D13/SCK, J3.pin_0, R1.Pin_1
  VCC: J1.vcc, J2.vcc, VCC1.+
